# Fritzing sketch RadarPi (saved by Fritzing 0.9.3b)
stripboards: 1

parts:
  Raspberry_Pi_1 = Raspberry Pi 3 [part_number=RPI-3-V1.2]
  U1 = 3.5mm Audio Jack [package=audio-jack-3.5mm-smd]
  Part1 = Adafruit MAX9814 Electret Microphone Amplifier [part_number="Adafruit #1713"]
  SPKR1 = Loudspeaker
  Part2 = Adafruit MAX98357A I2S 3W Class D Amplifier [part_number="Adafruit #3006"]
  C2 = Electrolytic Capacitor [capacitance=1µF package="100 mil [THT, electrolytic]"]

nets:
  GND: Raspberry_Pi_1.GND, U1.SLEEVE, U1.LEFT, Part1.GND, Part2.GND
  N1: Raspberry_Pi_1.GIPO19, Part2.LRCLK
  N2: Raspberry_Pi_1.GIPO21, Part2.DIN
  N3: Raspberry_Pi_1.GIPO18, Part2.BCLK
  5V: Raspberry_Pi_1.5V, Part1.VDD, Part2.VIN
  N4: U1.RIGHT, C2.-
  N5: Part1.OUTPUT, C2.+
  N6: SPKR1.pin2, Part2.SD_MODE

notes:
  USB Sound Card

custom parts:
  Adafruit MAX9814 Electret Microphone Amplifier: Add an ear to your project with this well-designed electret microphone amplifier with AGC. This fully assembled and tested board comes with a 20-20KHz electret microphone soldered on. For the amplification, we use the Maxim MAX9814, a specialty chip that is designed for amplifying electret microphones in situations where the loudness of the audio isn't predictable. This fancy microphone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
  Adafruit MAX98357A I2S 3W Class D Amplifier: Listen to this good news - we now have an all in one digital audio amp breakout board that works incredibly well with the Raspberry Pi! If you're looking for an easy and low cost way to get you digital sound files bumpin' then the MAX08357 I2S Amp Breakout is for you. It takes standard I2S digital audio input and, not only decodes it into analog, but also amplifies it directly into a speaker.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
